# Fritzing sketch RFID_ESP (saved by Fritzing 0.9.2b)
breadboards: 2

parts:
  U1 = NodeMCU V1.0
  Onderdeel1 = RFID-RC522-v2

nets:
  N1: U1.D3, Onderdeel1.SDA
  N2: U1.D4, Onderdeel1.GND
  N3: U1.GND, Onderdeel1.RST
  N4: U1.D5, Onderdeel1.SCK
  N5: U1.D6, Onderdeel1.MISO
  N6: U1.D7, Onderdeel1.MOSI
  3V3: U1.3V3, Onderdeel1.3.3V

custom parts:
  NodeMCU V1.0: ESP9266 based NodeMCU
  RFID-RC522-v2: A simple China made RFID-RC522 Reader; do check the pin labels, as this is a MFRC522 based clone.
